# Fritzing sketch Joystick+LED (saved by Fritzing 1.0.4)
breadboards: 1

parts:
  Част1 = Arduino Uno (Rev3)
  R1 = Resistor [tolerance=±5% resistance=220 power=0.25W package=THT]
  Част2 = Black Joystick KY-023
  LED1 = LED - 5mm [color="Red (633nm)" current=0.030A package="5 mm [THT]"]

nets:
  N1: Част1.A0, Част2.VRx
  N2: Част1.A1, Част2.VRy
  N3: Част1.D2, Част2.SW
  N4: Част1.D3_PWM, R1.Pin_0
  5V: Част1.5V, Част2.+5V
  GND: Част1.GND, Част2.GND, LED1.cathode
  N5: R1.Pin_1, LED1.anode

custom parts:
  Black Joystick KY-023: Description: The joystick is a combination of 2 analoog potentiometer and a digital switch. Arduino GND --> Module pin - Arduino +5V --> Module pin +5V Arduino Analoog 0 --> Module VRx Arduino Analoog 1 --> Module VRy Arduino Digital --> Module SW Dimensions: 1" x 1.25"
