# Fritzing sketch Joystick+RGB (saved by Fritzing 0.9.3b)
breadboards: 1

parts:
  Част1 = Arduino Uno (Rev3)
  R1 = Resistor [tolerance=±5% resistance=220 package=THT]
  R2 = Resistor [tolerance=±5% resistance=220 package=THT]
  R3 = Resistor [tolerance=±5% resistance=220 package=THT]
  LED1 = RGB LED (com. cathode, rgb) [package="5 mm [THT]"]
  Част2 = Black Joystick KY-023

nets:
  N1: Част1.A0, Част2.VRx
  N2: Част1.A1, Част2.VRy
  GND: Част1.GND, LED1.common_cathode, Част2.GND
  N3: Част1.D2, Част2.SW
  N4: Част1.D3_PWM, R1.Pin_0
  N5: Част1.D5_PWM, R2.Pin_0
  N6: Част1.D6_PWM, R3.Pin_0
  5V: Част1.5V, Част2.+5V
  N7: R1.Pin_1, LED1.red_anode
  N8: R2.Pin_1, LED1.green_anode
  N9: R3.Pin_1, LED1.blue_anode

custom parts:
  Black Joystick KY-023: Description: The joystick is a combination of 2 analoog potentiometer and a digital switch. Arduino GND --> Module pin - Arduino +5V --> Module pin +5V Arduino Analoog 0 --> Module VRx Arduino Analoog 1 --> Module VRy Arduino Digital --> Module SW Dimensions: 1" x 1.25"
